// Logisim project Atividade_UART.circ as structural Verilog: 4 circuits, main circuit main
module main (
  input  [7:0] in_1,
  input  in_2,
  output [7:0] out_3
);

  wire clock_1_out, clock_2_out, tx_1_out_4;

  Clock clock_1 (.out(clock_1_out));
  TX tx_1 (.CLK(clock_1_out), .Entrada_8b(in_1), .Seletor(in_2), .out_4(tx_1_out_4));
  Clock clock_2 (.out(clock_2_out));
  RX rx_1 (.in_1(tx_1_out_4), .in_2(clock_2_out), .Saida_8b(out_3));
endmodule

module TX (
  input  CLK,
  input  [7:0] Entrada_8b,
  input  Seletor,
  output out_4
);

  wire d_ff_1_q, d_ff_2_q, d_ff_3_q, d_ff_4_q, d_ff_5_q, d_ff_6_q, d_ff_7_q, multiplexer_1_out,
       multiplexer_2_out, multiplexer_3_out, multiplexer_4_out, multiplexer_5_out, multiplexer_6_out,
       multiplexer_7_out, multiplexer_8_out;

  Multiplexer multiplexer_1 (.in0(1'b0), .in1(Entrada_8b[0]), .out(multiplexer_1_out), .sel(Seletor));
  D_Flip_Flop d_ff_1 (.D(multiplexer_1_out), .clk(CLK), .Q(d_ff_1_q));  // open: Qn, preset, reset
  D_Flip_Flop d_ff_2 (.D(multiplexer_2_out), .clk(CLK), .Q(d_ff_2_q));  // open: Qn, preset, reset
  Multiplexer multiplexer_2 (.in0(d_ff_1_q), .in1(Entrada_8b[1]), .out(multiplexer_2_out), .sel(Seletor));
  D_Flip_Flop d_ff_3 (.D(multiplexer_3_out), .clk(CLK), .Q(d_ff_3_q));  // open: Qn, preset, reset
  Multiplexer multiplexer_3 (.in0(d_ff_2_q), .in1(Entrada_8b[2]), .out(multiplexer_3_out), .sel(Seletor));
  D_Flip_Flop d_ff_4 (.D(multiplexer_4_out), .clk(CLK), .Q(d_ff_4_q));  // open: Qn, preset, reset
  Multiplexer multiplexer_4 (.in0(d_ff_3_q), .in1(Entrada_8b[3]), .out(multiplexer_4_out), .sel(Seletor));
  D_Flip_Flop d_ff_5 (.D(multiplexer_5_out), .clk(CLK), .Q(d_ff_5_q));  // open: Qn, preset, reset
  Multiplexer multiplexer_5 (.in0(d_ff_4_q), .in1(Entrada_8b[4]), .out(multiplexer_5_out), .sel(Seletor));
  D_Flip_Flop d_ff_6 (.D(multiplexer_6_out), .clk(CLK), .Q(d_ff_6_q));  // open: Qn, preset, reset
  Multiplexer multiplexer_6 (.in0(d_ff_5_q), .in1(Entrada_8b[5]), .out(multiplexer_6_out), .sel(Seletor));
  Multiplexer multiplexer_7 (.in0(d_ff_6_q), .in1(Entrada_8b[6]), .out(multiplexer_7_out), .sel(Seletor));
  D_Flip_Flop d_ff_7 (.D(multiplexer_7_out), .clk(CLK), .Q(d_ff_7_q));  // open: Qn, preset, reset
  D_Flip_Flop d_ff_8 (.D(multiplexer_8_out), .clk(CLK), .Q(out_4));  // open: Qn, preset, reset
  Multiplexer multiplexer_8 (.in0(d_ff_7_q), .in1(Entrada_8b[7]), .out(multiplexer_8_out), .sel(Seletor));
endmodule

module RX (
  input  in_1,
  input  in_2,
  output [7:0] Saida_8b
);

  D_Flip_Flop d_ff_1 (.D(in_1), .clk(in_2), .Q(Saida_8b[0]));  // open: Qn, preset, reset
  D_Flip_Flop d_ff_2 (.D(Saida_8b[0]), .clk(in_2), .Q(Saida_8b[1]));  // open: Qn, preset, reset
  D_Flip_Flop d_ff_3 (.D(Saida_8b[1]), .clk(in_2), .Q(Saida_8b[2]));  // open: Qn, preset, reset
  D_Flip_Flop d_ff_4 (.D(Saida_8b[2]), .clk(in_2), .Q(Saida_8b[3]));  // open: Qn, preset, reset
  D_Flip_Flop d_ff_5 (.D(Saida_8b[3]), .clk(in_2), .Q(Saida_8b[4]));  // open: Qn, preset, reset
  D_Flip_Flop d_ff_6 (.D(Saida_8b[4]), .clk(in_2), .Q(Saida_8b[5]));  // open: Qn, preset, reset
  D_Flip_Flop d_ff_7 (.D(Saida_8b[5]), .clk(in_2), .Q(Saida_8b[6]));  // open: Qn, preset, reset
  D_Flip_Flop d_ff_8 (.D(Saida_8b[6]), .clk(in_2), .Q(Saida_8b[7]));  // open: Qn, preset, reset
endmodule

module Contador (
  input  CLK
);

  wire and_1_out, j_k_ff_1_q, j_k_ff_2_q, j_k_ff_3_q, j_k_ff_4_q;

  J_K_Flip_Flop #(.trigger("falling")) j_k_ff_1 (
    .J(1'b1), .K(1'b1), .clk(CLK), .Q(j_k_ff_1_q), .reset(and_1_out));  // open: Qn, preset
  J_K_Flip_Flop #(.trigger("falling")) j_k_ff_2 (
    .J(1'b1), .K(1'b1), .clk(j_k_ff_1_q), .Q(j_k_ff_2_q), .reset(and_1_out));  // open: Qn, preset
  J_K_Flip_Flop #(.trigger("falling")) j_k_ff_3 (
    .J(1'b1), .K(1'b1), .clk(j_k_ff_2_q), .Q(j_k_ff_3_q), .reset(and_1_out));  // open: Qn, preset
  and and_1 (and_1_out, j_k_ff_1_q, j_k_ff_4_q);
  J_K_Flip_Flop #(.trigger("falling")) j_k_ff_4 (
    .J(1'b1), .K(1'b1), .clk(j_k_ff_3_q), .Q(j_k_ff_4_q), .reset(and_1_out));  // open: Qn, preset
endmodule
