// Logisim project Full-Adder 4bits.circ as structural Verilog
module Half_Adder (
  input  A,
  input  B,
  output Cout,
  output Soma
);

  and and_1 (Cout, A, B);
  xor xor_1 (Soma, A, B);
endmodule

module Full_Adder (
  input  A,
  input  B,
  input  Cin,
  output Cout,
  output Soma
);

  wire half_adder_1_cout, half_adder_1_soma, half_adder_2_cout;

  Half_Adder half_adder_1 (.A(A), .B(B), .Cout(half_adder_1_cout), .Soma(half_adder_1_soma));
  Half_Adder half_adder_2 (.A(half_adder_1_soma), .B(Cin), .Cout(half_adder_2_cout), .Soma(Soma));
  or or_1 (Cout, half_adder_1_cout, half_adder_2_cout);
endmodule

module Full_Adder_4bits (
  input  A1,
  input  A2,
  input  A3,
  input  A4,
  input  Cin,
  input  B1,
  input  B2,
  input  B3,
  input  B4,
  output Cout,
  output Soma1,
  output Soma2,
  output Soma3,
  output Soma4
);

  wire full_adder_1_cout, full_adder_2_cout, full_adder_3_cout;

  Full_Adder full_adder_1 (.A(A1), .B(B1), .Cin(Cin), .Cout(full_adder_1_cout), .Soma(Soma1));
  Full_Adder full_adder_2 (.A(A2), .B(B2), .Cin(full_adder_1_cout), .Cout(full_adder_2_cout), .Soma(Soma2));
  Full_Adder full_adder_3 (.A(A3), .B(B3), .Cin(full_adder_2_cout), .Cout(full_adder_3_cout), .Soma(Soma3));
  Full_Adder full_adder_4 (.A(A4), .B(B4), .Cin(full_adder_3_cout), .Cout(Cout), .Soma(Soma4));
endmodule
